# Fritzing sketch garden (saved by Fritzing 0.9.3b)
circuit board: 6.6cm x 3.05cm

parts:
  IC1 = IC, DIP package, 16 pins [chip_label=IC]
  2 = female pin header, 3 pins [form="♀ (female)"]
  1 = female pin header, 3 pins [form="♀ (female)"]
  3 = female pin header, 3 pins [form="♀ (female)"]
  0 = female pin header, 3 pins [form="♀ (female)"]
  L = female pin header, 4 pins [form="♀ (female)"]
  A_G_V = female pin header, 4 pins [form="♀ (female)"]
  WeMos_D1_Mini1 = WeMos D1 Mini
  5V = female pin header, 3 pins [form="♀ (female)"]
  D0 = female pin header, 1 pin [form="♀ (female)"]

nets:
  N1: IC1.pin3, WeMos_D1_Mini1.A0
  N2: IC1.pin6, IC1.pin7, IC1.pin8, 2.pin1, 1.pin1, 3.pin1, 0.pin1, L.pin3, A_G_V.pin3, WeMos_D1_Mini1.G, 5V.pin3
  N3: IC1.pin9, WeMos_D1_Mini1.D5
  N4: IC1.pin10, WeMos_D1_Mini1.D6
  N5: IC1.pin11, WeMos_D1_Mini1.D7
  N6: IC1.pin12, 3.pin3
  N7: IC1.pin13, 0.pin3
  N8: IC1.pin14, 1.pin3
  N9: IC1.pin15, 2.pin3
  N10: IC1.pin16, 2.pin2, 1.pin2, 3.pin2, 0.pin2, L.pin4, A_G_V.pin4, WeMos_D1_Mini1.3V3
  N11: L.pin1, A_G_V.pin1, WeMos_D1_Mini1.D1
  N12: L.pin2, A_G_V.pin2, WeMos_D1_Mini1.D2
  N13: WeMos_D1_Mini1.5V, 5V.pin1
  N14: WeMos_D1_Mini1.D0, D0.pin1
